# Fritzing sketch Fritzing Sketch (saved by Fritzing 0.9.3b)

parts:
  Part1 = Arduino Pro Mini 328 - 3.3 V/8MHz
  Part2 = Bluetooth HC-05 Macho
  Part3 = BMP180 Breakout (GY-68)
  Part4 = Tri-Axis Gyro Breakout - L3G4200D
  Grove1 = Grove OLED 128x96
  BAT2 = Battery Holders [package=battcon_12mm]
  BAT3 = Battery Holders [package=battcon_12mm]
  BAT4 = Battery Holders [package=battcon_12mm]
  R1 = Resistor [tolerance=±5% resistance=10k package="0402 [SMD]"]
  R2 = Resistor [tolerance=±5% resistance=10k package="0402 [SMD]"]
  S2 = Pushbutton [package="[SMD]"]
  S4 = Pushbutton [package="[SMD]"]
  S5 = Toggle Switch [package=THT]
  R3 = Resistor [tolerance=±5% resistance=1k package=THT]

nets:
  GND: Part1.BLK, Part1.GND, Part2.GND, Part3.GND, Part4.GND, Grove1.GND, BAT4.-, R2.Pin_1, R3.Pin_1
  N1: Part1.A4, Part3.SDA, Part4.SDA, Grove1.SDA
  N2: Part1.A5, Part3.SCL, Part4.SCL, Grove1.SCL
  VCC: Part1.RAW, Part1.D8, Part1.D7, Part2.VCC, Part3.VCC, Part4.VCC, Grove1.VCC, R1.Pin_0, S2.Pin_3, S2.Pin_4, S4.Pin_3, S4.Pin_4, S5.COM
  N3: Part1.A0, R1.Pin_1, R2.Pin_0
  N4: Part1.D1/RX, Part2.TXD
  N5: Part1.D0/TX, Part2.RXD
  N6: BAT2.+, S5.L2
  N7: BAT2.-, BAT3.+
  N8: BAT3.-, BAT4.+
  N9: S2.Pin_1, S2.Pin_2, S4.Pin_2, R3.Pin_0

custom parts:
  Arduino Pro Mini 328 - 3.3 V/8MHz: Versión de Arduino Pro Mini basada en MEGA328P a 8MHz y alimentada a 3.3 voltios.
  BMP180 Breakout (GY-68): This is a simple breakout board for the BMP180, a high-precision, low-power barometric pressure sensor made by Bosch Sensortec. The range of measurement is from 300hPa to 1100hPa. The sensor can be supplied with voltage ranging from 1.8V to 3.6V. Operating temperature range is -40 to +85 °C. This particular breakout board (or perhaps the configuration) is produced by Shenzhen Keep Power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
